// Logisim project eyer_egalahmed.circ as structural Verilog: 11 circuits, main circuit Add1bit
module Add1bit (
  input  a_i,
  input  b_i,
  input  c_i,
  output r_o,
  output c_o
);

  wire and_1_out, and_2_out, and_3_out, xor_1_out;

  and and_1 (and_1_out, a_i, b_i);
  and and_2 (and_2_out, a_i, c_i);
  and and_3 (and_3_out, b_i, c_i);
  xor xor_1 (xor_1_out, a_i, b_i);
  xor xor_2 (r_o, xor_1_out, c_i);
  or or_1 (c_o, and_1_out, and_2_out, and_3_out);
endmodule

module Add4bits (
  input  c_i,
  input  [3:0] a_i,
  input  [3:0] b_i,
  output [3:0] r_o,
  output c_o
);

  wire C1, C2, C3;

  Add1bit add1bit_1 (.a_i(a_i[0]), .b_i(b_i[0]), .c_i(c_i), .r_o(r_o[0]), .c_o(C1));
  Add1bit add1bit_2 (.a_i(a_i[1]), .b_i(b_i[1]), .c_i(C1), .r_o(r_o[1]), .c_o(C2));
  Add1bit add1bit_3 (.a_i(a_i[2]), .b_i(b_i[2]), .c_i(C2), .r_o(r_o[2]), .c_o(C3));
  Add1bit add1bit_4 (.a_i(a_i[3]), .b_i(b_i[3]), .c_i(C3), .r_o(r_o[3]), .c_o(c_o));
endmodule

module AddSub (
  input  op_i,
  input  [3:0] a_i,
  input  [3:0] b_i,
  output [3:0] r_o,
  output carry_o
);

  wire [3:0] xor_1_out;

  xor xor_1 (xor_1_out[0], b_i[0], op_i);
  xor xor_2 (xor_1_out[1], b_i[1], op_i);
  xor xor_3 (xor_1_out[2], b_i[2], op_i);
  xor xor_4 (xor_1_out[3], b_i[3], op_i);
  Add4bits add4bits_1 (.c_i(op_i), .a_i(a_i), .b_i(xor_1_out), .r_o(r_o), .c_o(carry_o));
endmodule

module Calculation (
  input  op_i,
  input  [3:0] a_i,
  input  [3:0] b_i,
  output [3:0] r_o,
  output zero_o,
  output carry_o,
  output negative_o,
  output overflow_o
);

  wire and_1_out, and_2_out, xor_1_out;

  AddSub addsub_1 (.op_i(op_i), .a_i(a_i), .b_i(b_i), .r_o({negative_o, r_o[2:0]}), .carry_o(carry_o));
  // NoConnect on a_i[0]
  // NoConnect on a_i[1]
  // NoConnect on a_i[2]
  // NoConnect on b_i[0]
  // NoConnect on b_i[1]
  // NoConnect on b_i[2]
  xor xor_1 (xor_1_out, op_i, b_i[3]);
  nor nor_1 (zero_o, r_o[0], r_o[1], r_o[2], negative_o);
  and and_1 (and_1_out, ~a_i[3], ~xor_1_out, negative_o);  // AND_Gate
  or or_1 (overflow_o, and_1_out, and_2_out);
  and and_2 (and_2_out, a_i[3], xor_1_out, ~negative_o);  // AND_Gate

  assign r_o[3] = negative_o;
endmodule

module Comp (
  input  negative_i,
  input  overflow_i,
  input  zero_i,
  input  carry_i,
  input  [2:0] op_i,
  input  [3:0] a_i,
  input  [3:0] b_i,
  output cmp_o
);

  wire and_1_out, not_1_out, not_2_out, not_3_out, xor_1_out;

  // NoConnect on a_i
  // NoConnect on b_i
  xor xor_1 (xor_1_out, negative_i, overflow_i);
  not not_1 (not_1_out, zero_i);
  not not_2 (not_2_out, carry_i);
  not not_3 (not_3_out, xor_1_out);
  and and_1 (and_1_out, not_3_out, not_1_out);
  Multiplexer #(.select(3)) multiplexer_1 (
    .in0(1'b0), .in1(and_1_out), .in2(xor_1_out), .in3(not_1_out), .in4(carry_i), .in5(zero_i),
    .in6(not_2_out), .in7(1'b0), .out(cmp_o), .sel(op_i));
endmodule

module Arithmetic_selection (
  input  op_i,
  input  [3:0] calculation_i,
  input  comp_i,
  output [3:0] arith_sel_o
);

  Multiplexer #(.width(4)) multiplexer_1 (.in0(calculation_i), .in1({3'b000, comp_i}), .out(arith_sel_o), .sel(op_i));
endmodule

module Arithmetic (
  input  op_i,
  input  [3:0] a_i,
  input  [3:0] b_i,
  output carry_o,
  output overflow_o,
  output [3:0] arith_o
);

  Calculation calculation_1 ();  // open: op_i, a_i, b_i, r_o, zero_o, carry_o, negative_o, overflow_o
  Comp comp_1 ();  // open: negative_i, overflow_i, zero_i, carry_i, op_i, a_i, b_i, cmp_o
  Arithmetic_selection arithmetic_selection_1 ();  // open: op_i, calculation_i, comp_i, arith_sel_o

  // Notes on the sheet:
  //   A vous de régler le nombre de bits pour l'opcode (supprimez ensuite ce texte)
endmodule

module Logic (
  input  op_i,
  input  [3:0] a_i,
  input  [3:0] b_i,
  output [3:0] f_o
);


  // Notes on the sheet:
  //   A vous de régler le nombre de bits pour l'opcode (supprimez ensuite ce texte)
  //   NE PAS MODIFIER L'ORDRE DES ENTREES
endmodule

module OutputHandling (
  output [3:0] c_o,
  output error_o
);
endmodule

module ALU (
  input  [5:0] op_i,
  input  [3:0] a_i,
  input  [3:0] b_i,
  output [3:0] c_o,
  output error_o
);


  // Notes on the sheet:
  //   NE PAS MODIFIER L'ORDRE DES ENTREES
endmodule

module ALU_top (
  input  [5:0] op_i,
  input  [3:0] a,
  input  [3:0] b,
  output [3:0] c_o,
  output error_o
);

  ALU ALU_1 (.op_i(op_i), .a_i(a), .b_i(b), .c_o(c_o), .error_o(error_o));

  // Notes on the sheet:
  //   NE PAS MODIFIER !!!!
endmodule
